# Fritzing sketch lcdfritzing (saved by Fritzing 0.9.3b)
breadboards: 1

parts:
  Raspberry_Pi_1 = Raspberry Pi 3 [part_number=RPI-3-V1.2]
  LCD1 = LCD screen
  R2 = Trimmer Potentiometer [maximum_resistance=10kΩ package=THT]

nets:
  N1: Raspberry_Pi_1.GPIO27, LCD1.DB0
  N2: Raspberry_Pi_1.GPIO22, LCD1.DB1
  N3: Raspberry_Pi_1.GPIO5, LCD1.DB2
  N4: Raspberry_Pi_1.GPIO6, LCD1.DB3
  N5: Raspberry_Pi_1.GPIO13, LCD1.DB4
  N6: Raspberry_Pi_1.GPIO26, LCD1.DB5
  N7: Raspberry_Pi_1.GPIO16, LCD1.DB7
  N8: Raspberry_Pi_1.GPIO25, LCD1.RS
  N9: Raspberry_Pi_1.GPIO24, LCD1.E
  GND: Raspberry_Pi_1.GND, LCD1.VSS, LCD1.R/W, R2.leg1
  N10: Raspberry_Pi_1.GPIO18, LCD1.DB6
  5V: Raspberry_Pi_1.5V, LCD1.VDD, LCD1.LED+, R2.leg2
  N11: LCD1.V0, R2.wiper
